// Logisim project Decidotron.circ as structural Verilog: 1 circuit, main circuit main
module main (
  input  Pinapple,
  input  Peperoni,
  input  in_3,
  input  Bacon,
  input  GREEN_STUFF,
  input  Olives,
  input  in_7
);

  wire and_1_out, and_2_out, not_1_out, not_2_out, not_3_out, or_1_out;

  and and_1 (and_1_out, Pinapple, Peperoni, in_3);
  not not_1 (not_1_out, GREEN_STUFF);
  not not_2 (not_2_out, Olives);
  not not_3 (not_3_out, in_7);
  and and_2 (and_2_out, not_1_out, not_2_out, not_3_out);
  or or_1 (or_1_out, and_1_out, Bacon);
  // AND_Gate and_3 has open pins: in0=or_1_out, in1=and_2_out, out=open

  // Notes on the sheet:
  //   BBQ(0)/Red Sauce(1)?
  //   Small(0)/ Large (1)?
  //   Is Your Favorite Type Of Pizza Good?
endmodule
