// Logisim project LogicGates.circ as structural Verilog: 1 circuit, main circuit main
module main (
  input  in_1,
  input  in_2,
  input  in_3,
  input  in_4,
  input  in_5,
  input  in_6,
  input  in_7,
  input  in_8,
  input  in_9,
  input  in_10,
  input  in_11,
  input  in_12,
  input  in_13,
  input  in_14,
  output out_15,
  output out_16,
  output out_17,
  output out_18,
  output out_19,
  output out_20,
  output out_21,
  output out_22
);

  wire and_1_out, nand_1_out, nand_2_out, nand_3_out, nor_1_out, nor_2_out, nor_3_out, or_1_out,
       pull_resistor_3_node, transistor_2_out;

  and and_1 (and_1_out, in_7, in_9);
  Transistor transistor_1 (.in(1'b1), .out(out_15), .gate(in_1));
  Pull_Resistor pull_resistor_1 (.node(out_15));
  Transistor #(.\type ("n")) transistor_2 (.in(out_18), .out(transistor_2_out), .gate(in_4));
  Pull_Resistor pull_resistor_2 (.node(out_18));
  not not_1 (out_19, and_1_out);
  nor nor_1 (nor_1_out, in_11, in_13);
  nor nor_2 (nor_2_out, in_11, nor_1_out);
  nor nor_3 (nor_3_out, nor_1_out, in_13);
  nor nor_4 (out_21, nor_2_out, nor_3_out);
  Pull_Resistor pull_resistor_3 (.node(pull_resistor_3_node));
  Transistor #(.\type ("n")) transistor_3 (.in(1'b1), .out(pull_resistor_3_node), .gate(in_2));
  or or_1 (or_1_out, in_8, in_10);
  not not_2 (out_20, or_1_out);
  Transistor #(.\type ("n")) transistor_4 (.in(pull_resistor_3_node), .out(out_16), .gate(in_3));
  Transistor #(.\type ("n")) transistor_5 (.in(1'b1), .out(out_17), .gate(in_5));
  Pull_Resistor pull_resistor_4 (.node(out_17));
  Transistor #(.\type ("n"), .gate("br")) transistor_6 (.in(1'b1), .out(out_17), .gate(in_6));
  Pull_Resistor pull_resistor_5 (.node(out_17));
  Pull_Resistor pull_resistor_6 (.node(out_16));
  nand nand_1 (nand_1_out, in_12, in_14);
  nand nand_2 (nand_2_out, in_12, nand_1_out);
  nand nand_3 (nand_3_out, nand_1_out, in_14);
  nand nand_4 (out_22, nand_2_out, nand_3_out);
  // also tied to GND on the sheet: transistor_2_out
  // also tied to VCC on the sheet: out_18

  // Notes on the sheet:
  //   Not Gate P
  //   Not Gate N
  //   NAND Gate
  //   XNOR Gate
  //   NOR Gate
  //   And Gate
  //   OR Gate
  //   XOR Gate
endmodule
